# Fritzing sketch Schema (saved by Fritzing 1.0.5)
perfboards: 1

parts:
  Waage = HX711 Weighing Sensor Module
  Q1 = TRANSISTOR_NPN [package=to-92-ammo]
  Q2 = TRANSISTOR_NPN [package=to-92-ammo]
  J1 = Basic Servo
  M1 = RioRand LM2596
  V1 = DC Power [voltage=12V internal_resistance=0.1Ω]
  Oled = Grove OLED 128x96
  Arduino = Arduino Uno (Rev3)
  LED1 = LED - 5mm [color="Red (633nm)" current=0.030A package="5 mm [THT]"]
  LED2 = LED - 5mm [color="Green (560nm)" current=0.030A package="5 mm [THT]"]
  R1 = Resistor [tolerance=±5% power=0.25W resistance=330 package=THT]
  R2 = Resistor [tolerance=±5% power=0.25W resistance=220 package=THT]
  R3 = Resistor [tolerance=±5% power=0.25W resistance=220 package=THT]
  R4 = Resistor [tolerance=±5% power=0.25W resistance=220 package=THT]
  Button_Plus = Round Pushbutton
  Button_Minus = Round Pushbutton
  Button_Start = Round Pushbutton
  8V_In = Screw terminal - 2 pins [package=THT]
  Display = screw terminal, 4 pins
  Led_Red = Screw terminal - 2 pins [package=THT]
  Led_Green = Screw terminal - 2 pins [package=THT]
  Btn_+ = Screw terminal - 2 pins [package=THT]
  Btn_- = Screw terminal - 2 pins [package=THT]
  Btn_Start = Screw terminal - 2 pins [package=THT]
  Servo = screw terminal, 3 pins
  Scale = screw terminal, 4 pins
  Load_Cell1 = Load Cell - Red/white/black/green
  R5 = Resistor [tolerance=±5% power=0.25W resistance=220 package=THT]

nets:
  5V: Waage.VCC, Arduino.5V, R1.Pin_1, R2.Pin_1
  GND: Waage.GND, Q1.E, Q2.E, J1.gnd, M1.Pin_4, Oled.GND, Arduino.GND, Button_Plus.leg0, Button_Minus.leg0, Button_Start.leg0, 8V_In.pin1, Display.pin1, Btn_+.pin2, Btn_-.pin2, Btn_Start.pin2, Servo.pin3
  N1: Waage.DO/RX, Arduino.D2
  N2: Waage.CK/TX, Arduino.D3_PWM
  N3: Waage.E+, Scale.pin4, Load_Cell1.wire1
  N4: Waage.E-, Scale.pin3, Load_Cell1.wire3
  N5: Waage.A+, Scale.pin2, Load_Cell1.wire2
  N6: Waage.A-, Scale.pin1, Load_Cell1.wire4
  N7: Q1.B, R4.Pin_1
  N8: Q1.C, LED2.cathode, Led_Green.pin1
  N9: Q2.B, R3.Pin_1
  N10: Q2.C, LED1.cathode, Led_Red.pin1
  8V: J1.vcc, M1.Pin_3, Arduino.VIN, 8V_In.pin2, Servo.pin2
  N11: J1.pulse, Servo.pin1, R5.Pin_1
  N12: M1.Pin_1, V1.V+
  N13: M1.Pin_2, V1.V-
  VCC: Oled.VCC, Arduino.3V3, Display.pin2
  N14: Oled.SDA, Arduino.A4/SDA, Display.pin4
  N15: Oled.SCL, Arduino.A5/SCL, Display.pin3
  N16: Arduino.A0, Button_Start.leg1, Btn_Start.pin1
  N17: Arduino.A1, Button_Minus.leg1, Btn_-.pin1
  N18: Arduino.A2, Button_Plus.leg1, Btn_+.pin1
  N19: Arduino.D4, R3.Pin_0
  N20: Arduino.D5_PWM, R4.Pin_0
  N21: Arduino.D6_PWM, R5.Pin_0
  N22: LED1.anode, R1.Pin_0, Led_Red.pin2
  N23: LED2.anode, R2.Pin_0, Led_Green.pin2

custom parts:
  Load Cell - Red/white/black/green: A rectangle load cell/weighting pressure Sensor with four wires - Red, white, black, green. Normally corresponding with E+, E-, A+, A- respectively.
